# Fritzing sketch pacman_clock (saved by Fritzing 0.9.3b)

parts:
  Part1 = Arduino Mega ADK (Rev3)
  ZS-042_RTC1 = ZS-042 RTC Module
  S1 = Momentary Switch [package=ksa_sealed_tac_switch]
  S2 = Momentary Switch [package=ksa_sealed_tac_switch]

nets:
  N1: Part1.D21/SCL, ZS-042_RTC1.SCL
  N2: Part1.D20/SDA, ZS-042_RTC1.SDA
  GND: Part1.GND, ZS-042_RTC1.GND, S1.1
  N3: Part1.D8_PWM, S1.2
  5V: Part1.5V, ZS-042_RTC1.VCC
  N4: Part1.D7_PWM, S2.4
